# Fritzing sketch diagram_L298N (saved by Fritzing 0.9.10b)

parts:
  Composant1 = Arduino Nano (Rev3.0)
  J5 = male pin header, 2 pins [form="♂ (male)"]
  L298N1 = L298N DC motor driver
  M2 = DC Motor [voltage_(max)=6V voltage_(min)=3V]
  S3 = Momentary Switch [package=ksa_sealed_tac_switch]
  M3 = INA219 DC Current Monitor Module [part_number=CJMCU]
  S5 = Momentary Switch [package=ksa_sealed_tac_switch]
  D1 = Rectifier Diode [part_number=1N4001 package="Melf DO-213 AA [SMD]"]

nets:
  GND: Composant1.GND, S3.2, M3.GND, S5.2
  N1: Composant1.D2, S5.3
  N2: Composant1.D3, S3.3
  N3: Composant1.D7, L298N1.IN2
  N4: Composant1.D8, L298N1.IN1
  N5: Composant1.D9, L298N1.ENA
  5V: Composant1.5V, M3.VCC
  N6: Composant1.A5, M3.SCL
  N7: Composant1.A4, M3.SDA
  N8: J5.pin1, D1.anode
  N9: J5.pin2, L298N1.GND
  N10: L298N1.OUT1, M2.pin_2
  N11: L298N1.OUT2, M3.Vin+
  N12: L298N1.12V, D1.cathode
  N13: M2.pin_1, M3.Vin-

notes:
  +12V max
  Gnd
  +5V
  S (D2)
  Vin 7V-12V
  Gnd commun
  S (A0)
  V motor +2V ou +2.6V si diode
  controler (D13)
  Chris74
  L298N Motor Driver Board
  INA219 current sensor
  bouton -
  bouton +
  DC motor
  Gnd com
  Arduino ebike e-shifter

custom parts:
  L298N DC motor driver: 2x DC motor driver with 78M05 positive voltage regulator (7..35 V) L298N: max 46 V, 2 A Set 5 V Enable jumper to enable 5 V regultor (needed for the L298N) and +5 V output at screw terminal or supply external +5 V at screw terminal Set ENA and/or ENB to +5 V to enable motor permanently or supply ENA and/or ENB with PWM signal IN1 and IN2 set rotation directory for motor A (OUT1/OUT2) IN2 and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
  INA219 DC Current Monitor Module: INA219 DC Current Monitor Module Links: INA219 product information
